// Logisim project Lab3_ctrl_unit.circ as structural Verilog: 1 circuit, main circuit main
module main (
  input  [5:0] in_1
);

  wire and_1_out, and_2_out, and_3_out, and_4_out, not_1_out, not_2_out, not_3_out, not_4_out, not_5_out,
       not_6_out, not_7_out, not_8_out, not_9_out, not_10_out, not_11_out, not_12_out, not_13_out,
       not_14_out, not_15_out, not_16_out, or_1_out, or_2_out;

  not not_1 (not_1_out, in_1[3]);
  not not_2 (not_2_out, in_1[1]);
  not not_3 (not_3_out, in_1[0]);
  not not_4 (not_4_out, in_1[4]);
  not not_5 (not_5_out, in_1[2]);
  and and_1 (and_1_out, not_3_out, not_2_out, not_5_out, not_1_out, not_4_out, not_6_out);
  not not_6 (not_6_out, in_1[5]);
  not not_7 (not_7_out, in_1[3]);
  not not_8 (not_8_out, in_1[1]);
  not not_9 (not_9_out, in_1[2]);
  and and_2 (and_2_out, in_1[0], not_8_out, not_9_out, not_7_out, in_1[4], in_1[5]);
  not not_10 (not_10_out, in_1[1]);
  and and_3 (and_3_out, in_1[0], not_10_out, in_1[2], not_11_out, in_1[4], in_1[5]);
  not not_11 (not_11_out, in_1[3]);
  not not_12 (not_12_out, in_1[2]);
  not not_13 (not_13_out, in_1[0]);
  not not_14 (not_14_out, in_1[1]);
  and and_4 (and_4_out, not_13_out, not_14_out, not_12_out, in_1[3], not_16_out, not_15_out);
  not not_15 (not_15_out, in_1[5]);
  not not_16 (not_16_out, in_1[4]);
  or or_1 (or_1_out, and_3_out, and_2_out);
  or or_2 (or_2_out, and_2_out, and_1_out);
  LED RegDst (.in(and_1_out));
  LED ALUSrc (.in(or_1_out));
  LED MemToReg (.in(and_2_out));
  LED Reg_Write (.in(or_2_out));
  LED Mem_Read (.in(and_2_out));
  LED Mem_Write (.in(and_3_out));
  LED Branch (.in(and_4_out));
  LED ALUop1 (.in(and_1_out));
  LED ALUOp0 (.in(and_4_out));
endmodule
