// Logisim project full.circ as structural Verilog: 4 circuits, main circuit main
// Data 2
module main (
  input  [19:0] DATA_IN,
  input  [19:0] ALU_result,
  output [1:0] Opcode,
  output [19:0] DATA_OUT_1,
  output Carry_In,
  output Borrow_In,
  output [19:0] DATA_OUT_2
);

  wire BEQ_out, BNQ_out, CLOCK_out, comparator_1_eq, control_unit_1_alu_enable, control_unit_1_beq,
       control_unit_1_bnq, control_unit_1_jump_enable, control_unit_1_memwrite, control_unit_1_reg_write,
       not_1_out, not_2_out, or_1_out, or_2_out;
  wire [3:0] multiplexer_3_out;
  wire [9:0] rom_1_data;
  wire [17:10] rom_1_data_2;
  wire [19:0] adder_1_out, bit_extender_1_out, bit_extender_2_out, multiplexer_1_out, multiplexer_2_out,
       multiplexer_4_out, ram_1_data, register_1_q;

  Multiplexer #(.width(20), .enable("false")) multiplexer_1 (
    .in0(multiplexer_2_out), .in1(bit_extender_2_out), .out(multiplexer_1_out), .sel(or_2_out));
  Multiplexer #(.width(20), .enable("false")) multiplexer_2 (
    .in0(adder_1_out), .in1(bit_extender_1_out), .out(multiplexer_2_out), .sel(control_unit_1_jump_enable));
  Register #(.width(20)) register_1 (.D(multiplexer_1_out), .Q(register_1_q), .clk(CLOCK_out));  // open: en, clr
  Clock CLOCK (.out(CLOCK_out));
  Adder #(.width(20)) adder_1 (.a(register_1_q), .b(DATA_IN), .out(adder_1_out));  // open: cin, cout
  assign bit_extender_1_out = {{2{1'b0}}, {rom_1_data_2, rom_1_data}};  // Bit_Extender bit_extender_1
  assign bit_extender_2_out = {{10{1'b0}}, rom_1_data};  // Bit_Extender bit_extender_2
  ROM #(.addrWidth(20), .dataWidth(20)) rom_1 (
    .addr(register_1_q), .data({Opcode, rom_1_data_2, rom_1_data}));  // open: sel
  Multiplexer #(.width(4)) multiplexer_3 (
    .in0(rom_1_data_2[13:10]), .in1(rom_1_data_2[17:14]), .out(multiplexer_3_out),
    .sel(control_unit_1_memwrite));  // open: en
  control_unit control_unit_1 (
    .OPCode(Opcode), .Funct(rom_1_data[2:0]), .ALU_Enable(control_unit_1_alu_enable),
    .Jump_Enable(control_unit_1_jump_enable), .Reg_Write(control_unit_1_reg_write),
    .MemWrite(control_unit_1_memwrite), .BEQ(control_unit_1_beq), .BNQ(control_unit_1_bnq));
  Multiplexer #(.width(20), .enable("false")) multiplexer_4 (
    .in0(ram_1_data), .in1(ALU_result), .out(multiplexer_4_out), .sel(control_unit_1_alu_enable));
  Reg_File reg_file_1 (
    .Data_In(multiplexer_4_out), .RegWrite(control_unit_1_reg_write), .RD(rom_1_data_2[17:14]),
    .DATA_OUT_1(DATA_OUT_1), .DATA_OUT_2(DATA_OUT_2), .RT(rom_1_data[9:6]), .RS(multiplexer_3_out),
    .CLOCK(CLOCK_out));
  RAM #(.addrWidth(14), .dataWidth(20)) ram_1 (
    .addr({rom_1_data_2[13:10], rom_1_data}), .data(ram_1_data), .sel(or_1_out), .clk(CLOCK_out),
    .ld(not_1_out));  // open: clr
  not not_1 (not_1_out, control_unit_1_memwrite);
  ALU alu_1 (
    .RS(DATA_OUT_1), .RT(DATA_OUT_2), .ALU_OP(rom_1_data[2:0]), .ALU_result(ALU_result),
    .SHAMT(rom_1_data[5:3]), .Carry_In(Carry_In), .Borrow_In(Borrow_In));  // open: Carry_Out, Borrow_Out
  or or_1 (or_1_out, control_unit_1_reg_write, control_unit_1_memwrite);
  Comparator #(.width(20)) comparator_1 (.a(DATA_OUT_1), .b(DATA_OUT_2), .eq(comparator_1_eq));  // open: gt, lt
  and BEQ (BEQ_out, comparator_1_eq, control_unit_1_beq);
  not not_2 (not_2_out, comparator_1_eq);
  and BNQ (BNQ_out, not_2_out, control_unit_1_bnq);
  or or_2 (or_2_out, BEQ_out, BNQ_out);

  // Notes on the sheet:
  //   20 BIT SINGLE CYCLE CPU DATAPATH
  //   CONTROL UNIT
  //   REG FILE
  //   ALU
endmodule

module ALU (
  input  [19:0] RS,
  input  Carry_In,
  input  [19:0] RT,
  input  Borrow_In,
  input  [2:0] SHAMT,
  input  [2:0] ALU_OP,
  output Carry_Out,
  output Borrow_Out,
  output [19:0] ALU_result
);

  wire comparator_1_gt;
  wire [1:0] not_1_out;
  wire [19:0] adder_1_out, and_1_out, bit_extender_1_out, nor_1_out, or_1_out, shifter_1_out, shifter_2_out,
       subtractor_1_out;

  assign not_1_out = ~2'b11;  // NOT_Gate not_1, 2 bits wide
  Adder #(.width(20)) adder_1 (.a(RS), .b(RT), .out(adder_1_out), .cin(Carry_In), .cout(Carry_Out));
  Subtractor #(.width(20)) subtractor_1 (.a(RS), .b(RT), .out(subtractor_1_out), .bin(Borrow_In), .bout(Borrow_Out));
  assign and_1_out = RS & RT;  // AND_Gate and_1, 20 bits wide
  assign or_1_out = RS | RT;  // OR_Gate or_1, 20 bits wide
  Shifter #(.width(20)) shifter_1 (.in(RS), .\dist ({SHAMT, not_1_out}), .out(shifter_1_out));
  Shifter #(.width(20), .shift("lr")) shifter_2 (.in(RS), .\dist ({SHAMT, not_1_out}), .out(shifter_2_out));
  Comparator #(.width(20)) comparator_1 (.a(RS), .b(RT), .gt(comparator_1_gt));  // open: eq, lt
  assign nor_1_out = ~(RS | RT);  // NOR_Gate nor_1, 20 bits wide
  assign bit_extender_1_out = {{19{1'b0}}, comparator_1_gt};  // Bit_Extender bit_extender_1
  Multiplexer #(.select(3), .width(20), .enable("false")) multiplexer_1 (
    .in0(adder_1_out), .in1(subtractor_1_out), .in2(and_1_out), .in3(or_1_out), .in4(nor_1_out),
    .in5(shifter_1_out), .in6(shifter_2_out), .in7(bit_extender_1_out), .out(ALU_result), .sel(ALU_OP));

  // Notes on the sheet:
  //   ARITHMATIC LOGIC UNIT
endmodule

module Reg_File (
  input  [19:0] Data_In,
  input  RegWrite,
  input  [3:0] RS,
  input  [3:0] RD,
  input  [3:0] RT,
  input  CLOCK,
  output [19:0] DATA_OUT_1,
  output [19:0] DATA_OUT_2
);

  wire and_1_out, and_2_out, and_3_out, and_4_out, and_5_out, and_6_out, and_7_out, and_8_out, and_9_out,
       and_10_out, and_11_out, and_12_out, and_13_out, and_14_out, and_15_out, and_16_out, decoder_1_out0,
       decoder_1_out1, decoder_1_out2, decoder_1_out3, decoder_1_out4, decoder_1_out5, decoder_1_out6,
       decoder_1_out7, decoder_1_out8, decoder_1_out9, decoder_1_out10, decoder_1_out11, decoder_1_out12,
       decoder_1_out13, decoder_1_out14, decoder_1_out15;
  wire [19:0] register_1_q, register_2_q, register_3_q, register_4_q, register_5_q, register_6_q,
       register_7_q, register_8_q, register_9_q, register_10_q, register_11_q, register_12_q, register_13_q,
       register_14_q, register_15_q, register_16_q;

  Decoder #(.select(4)) decoder_1 (
    .out0(decoder_1_out0), .out1(decoder_1_out1), .out2(decoder_1_out2), .out3(decoder_1_out3),
    .out4(decoder_1_out4), .out5(decoder_1_out5), .out6(decoder_1_out6), .out7(decoder_1_out7),
    .out8(decoder_1_out8), .out9(decoder_1_out9), .out10(decoder_1_out10), .out11(decoder_1_out11),
    .out12(decoder_1_out12), .out13(decoder_1_out13), .out14(decoder_1_out14), .out15(decoder_1_out15),
    .sel(RD));  // open: en
  and and_1 (and_1_out, RegWrite, decoder_1_out0);
  and and_2 (and_2_out, RegWrite, decoder_1_out1);
  and and_3 (and_3_out, RegWrite, decoder_1_out2);
  and and_4 (and_4_out, RegWrite, decoder_1_out3);
  and and_5 (and_5_out, RegWrite, decoder_1_out4);
  and and_6 (and_6_out, RegWrite, decoder_1_out5);
  and and_7 (and_7_out, RegWrite, decoder_1_out6);
  and and_8 (and_8_out, RegWrite, decoder_1_out7);
  and and_9 (and_9_out, RegWrite, decoder_1_out8);
  and and_10 (and_10_out, RegWrite, decoder_1_out9);
  and and_11 (and_11_out, RegWrite, decoder_1_out10);
  and and_12 (and_12_out, RegWrite, decoder_1_out11);
  and and_13 (and_13_out, RegWrite, decoder_1_out12);
  and and_14 (and_14_out, RegWrite, decoder_1_out13);
  and and_15 (and_15_out, RegWrite, decoder_1_out14);
  and and_16 (and_16_out, RegWrite, decoder_1_out15);
  Register #(.width(20)) register_1 (.D(Data_In), .en(and_1_out), .Q(register_1_q), .clk(CLOCK));  // open: clr
  Register #(.width(20)) register_2 (.D(Data_In), .en(and_2_out), .Q(register_2_q), .clk(CLOCK));  // open: clr
  Register #(.width(20)) register_3 (.D(Data_In), .en(and_3_out), .Q(register_3_q), .clk(CLOCK));  // open: clr
  Register #(.width(20)) register_4 (.D(Data_In), .en(and_4_out), .Q(register_4_q), .clk(CLOCK));  // open: clr
  Register #(.width(20)) register_5 (.D(Data_In), .en(and_5_out), .Q(register_5_q), .clk(CLOCK));  // open: clr
  Register #(.width(20)) register_6 (.D(Data_In), .en(and_6_out), .Q(register_6_q), .clk(CLOCK));  // open: clr
  Register #(.width(20)) register_7 (.D(Data_In), .en(and_7_out), .Q(register_7_q), .clk(CLOCK));  // open: clr
  Register #(.width(20)) register_8 (.D(Data_In), .en(and_8_out), .Q(register_8_q), .clk(CLOCK));  // open: clr
  Register #(.width(20)) register_9 (.D(Data_In), .en(and_9_out), .Q(register_9_q), .clk(CLOCK));  // open: clr
  Register #(.width(20)) register_10 (.D(Data_In), .en(and_10_out), .Q(register_10_q), .clk(CLOCK));  // open: clr
  Register #(.width(20)) register_11 (.D(Data_In), .en(and_11_out), .Q(register_11_q), .clk(CLOCK));  // open: clr
  Register #(.width(20)) register_12 (.D(Data_In), .en(and_12_out), .Q(register_12_q), .clk(CLOCK));  // open: clr
  Register #(.width(20)) register_13 (.D(Data_In), .en(and_13_out), .Q(register_13_q), .clk(CLOCK));  // open: clr
  Register #(.width(20)) register_14 (.D(Data_In), .en(and_14_out), .Q(register_14_q), .clk(CLOCK));  // open: clr
  Register #(.width(20)) register_15 (.D(Data_In), .en(and_15_out), .Q(register_15_q), .clk(CLOCK));  // open: clr
  Register #(.width(20)) register_16 (.D(Data_In), .en(and_16_out), .Q(register_16_q), .clk(CLOCK));  // open: clr
  Multiplexer #(.select(4), .width(20), .enable("false")) multiplexer_1 (
    .in0(register_1_q), .in1(register_2_q), .in2(register_3_q), .in3(register_4_q), .in4(register_5_q),
    .in5(register_6_q), .in6(register_7_q), .in7(register_8_q), .in8(register_9_q), .in9(register_10_q),
    .in10(register_11_q), .in11(register_12_q), .in12(register_13_q), .in13(register_14_q),
    .in14(register_15_q), .in15(register_16_q), .out(DATA_OUT_1), .sel(RS));
  Multiplexer #(.select(4), .width(20), .enable("false")) multiplexer_2 (
    .in0(register_1_q), .in1(register_2_q), .in2(register_3_q), .in3(register_4_q), .in4(register_5_q),
    .in5(register_6_q), .in6(register_7_q), .in7(register_8_q), .in8(register_9_q), .in9(register_10_q),
    .in10(register_11_q), .in11(register_12_q), .in12(register_13_q), .in13(register_14_q),
    .in14(register_15_q), .in15(register_16_q), .out(DATA_OUT_2), .sel(RT));

  // Notes on the sheet:
  //   20 BIT REGISTER FILE
endmodule

module control_unit (
  input  [2:0] Funct,
  input  [1:0] OPCode,
  output MemWrite,
  output Reg_Write,
  output ALU_Enable,
  output BEQ,
  output BNQ,
  output Jump_Enable
);

  wire and_2_out, and_4_out, and_5_out, and_6_out, and_7_out, and_11_out;

  and and_1 (Jump_Enable, OPCode[1], ~OPCode[0]);  // AND_Gate
  and and_2 (and_2_out, ~OPCode[1], OPCode[0]);  // AND_Gate
  and and_3 (ALU_Enable, ~OPCode[1], ~OPCode[0]);  // AND_Gate
  and and_4 (and_4_out, ~Funct[2], ~Funct[1], ~Funct[0]);  // AND_Gate
  and and_5 (and_5_out, and_4_out, and_2_out);
  and and_6 (and_6_out, ~Funct[2], ~Funct[1], Funct[0]);  // AND_Gate
  or or_1 (Reg_Write, and_5_out, ALU_Enable);
  and and_7 (and_7_out, ~Funct[2], Funct[1], ~Funct[0]);  // AND_Gate
  and and_8 (MemWrite, and_6_out, and_2_out);
  and and_9 (BEQ, and_7_out, and_2_out);
  and and_10 (BNQ, and_11_out, and_2_out);
  and and_11 (and_11_out, ~Funct[2], Funct[1], Funct[0]);  // AND_Gate

  // Notes on the sheet:
  //   CONTROL UNIT
endmodule
