// Logisim project lab1soft.circ as structural Verilog: 1 circuit, main circuit main
module main (
  input  [15:0] Data_In,
  input  in_2,
  input  [15:0] data_out_1,
  input  [2:0] in_4,
  input  [2:0] in_5,
  input  [15:0] data_out_2,
  input  [2:0] in_7
);

  wire and_1_out, and_2_out, and_3_out, and_4_out, and_5_out, and_6_out, and_7_out, and_8_out, Clock_out,
       decoder_1_out1, decoder_1_out2, decoder_1_out3, decoder_1_out5, decoder_1_out6, decoder_1_out7;
  wire [15:0] register_1_q, register_2_q, register_3_q, register_4_q, register_5_q, register_6_q,
       register_7_q, register_8_q;

  Decoder #(.select(3)) decoder_1 (
    .out0(in_2), .out1(decoder_1_out1), .out2(decoder_1_out2), .out3(decoder_1_out3), .out4(in_2),
    .out5(decoder_1_out5), .out6(decoder_1_out6), .out7(decoder_1_out7), .sel(in_5));  // open: en
  and and_1 (and_1_out, in_2, in_2);
  and and_2 (and_2_out, in_2, decoder_1_out1);
  and and_3 (and_3_out, in_2, decoder_1_out2);
  and and_4 (and_4_out, in_2, decoder_1_out3);
  and and_5 (and_5_out, in_2, in_2);
  and and_6 (and_6_out, in_2, decoder_1_out5);
  and and_7 (and_7_out, in_2, decoder_1_out6);
  and and_8 (and_8_out, in_2, decoder_1_out7);
  Register #(.width(16)) register_1 (.D(Data_In), .en(and_1_out), .Q(register_1_q), .clk(Clock_out));  // open: clr
  Register #(.width(16)) register_2 (.D(Data_In), .en(and_2_out), .Q(register_2_q), .clk(Clock_out));  // open: clr
  Register #(.width(16)) register_3 (.D(Data_In), .en(and_3_out), .Q(register_3_q), .clk(Clock_out));  // open: clr
  Register #(.width(16)) register_4 (.D(Data_In), .en(and_4_out), .Q(register_4_q), .clk(Clock_out));  // open: clr
  Register #(.width(16)) register_5 (.D(Data_In), .en(and_5_out), .Q(register_5_q), .clk(Clock_out));  // open: clr
  Register #(.width(16)) register_6 (.D(Data_In), .en(and_6_out), .Q(register_6_q), .clk(Clock_out));  // open: clr
  Register #(.width(16)) register_7 (.D(Data_In), .en(and_7_out), .Q(register_7_q), .clk(Clock_out));  // open: clr
  Register #(.width(16)) register_8 (.D(Data_In), .en(and_8_out), .Q(register_8_q), .clk(Clock_out));  // open: clr
  Clock Clock (.out(Clock_out));
  Multiplexer #(.select(3), .width(16)) multiplexer_1 (
    .in0(register_1_q), .in1(register_2_q), .in2(register_3_q), .in3(register_4_q), .in4(register_5_q),
    .in5(register_6_q), .in6(register_7_q), .in7(register_8_q), .out(data_out_1), .sel(in_4));  // open: en
  Multiplexer #(.select(3), .width(16)) multiplexer_2 (
    .in0(register_1_q), .in1(register_2_q), .in2(register_3_q), .in3(register_4_q), .in4(register_5_q),
    .in5(register_6_q), .in6(register_7_q), .in7(register_8_q), .out(data_out_2), .sel(in_7));  // open: en
endmodule
