// Logisim project lab2soft.circ as structural Verilog: 5 circuits, main circuit main
// Data 2
module main (
  input  [5:0] Opcode,
  input  [23:0] in_2,
  input  [15:0] ALU_result,
  input  [15:0] Data_1,
  input  [2:0] Write_address,
  input  [2:0] Read_Register_1,
  input  [2:0] Read_register_2,
  input  [15:0] Data_2,
  input  in_9,
  input  [2:0] in_10
);

  wire clock_1_out;
  wire [23:0] adder_1_out, register_1_q;
  wire [25:0] rom_1_data;

  Register #(.width(24)) register_1 (.D(adder_1_out), .Q(register_1_q), .clk(clock_1_out));  // open: en, clr
  Clock clock_1 (.out(clock_1_out));
  Adder #(.width(24)) adder_1 (.a(register_1_q), .b(in_2), .out(adder_1_out));  // open: cin, cout
  ROM #(.addrWidth(24), .dataWidth(32)) rom_1 (
    .addr(register_1_q),
    .data({Opcode, rom_1_data[25:24], Read_register_2, rom_1_data[20:19], Read_Register_1, rom_1_data[15:14], Write_address, rom_1_data[10:0]}));  // open: sel
  control_unit Control_Unit (.in_1(Opcode), .RegWrite(in_9));  // open: ALUOp
  Reg_File Reg_File (
    .Data_In(ALU_result), .RegWrite(in_9), .Write_Address(Write_address), .data_out_1(Data_1),
    .data_out_2(Data_2), .Read_Registrar_2(Read_register_2), .Read_registrar_1(Read_Register_1),
    .in_8(clock_1_out));
  // ALU ALU: pin names not known; wires that end beside it: Data_1, Data_1
endmodule

module ALU (
  input  [15:0] Data_1,
  input  [15:0] Data_2,
  input  [15:0] ALU_result,
  input  [2:0] in_4
);

  wire [2:0] undriven;
  wire [15:0] adder_1_out, and_1_out, nor_1_out, not_1_out, or_1_out, subtractor_1_out, xor_1_out;

  Adder #(.width(16)) adder_1 (.a(Data_1), .b(Data_2), .out(adder_1_out));  // open: cin, cout
  Subtractor #(.width(16)) subtractor_1 (.b(Data_2), .out(subtractor_1_out));  // open: a, bin, bout
  assign and_1_out = Data_1 & Data_2;  // AND_Gate and_1, 16 bits wide
  assign or_1_out = Data_1 | Data_2;  // OR_Gate or_1, 16 bits wide
  assign xor_1_out = Data_1 ^ Data_2;  // XOR_Gate xor_1, 16 bits wide
  assign nor_1_out = ~(Data_1 | Data_2);  // NOR_Gate nor_1, 16 bits wide
  assign not_1_out = ~Data_1;  // NOT_Gate not_1, 16 bits wide
  Multiplexer #(.select(3), .width(16)) multiplexer_1 (
    .in0(adder_1_out), .in1(subtractor_1_out), .in2(and_1_out), .in3(or_1_out), .in4(xor_1_out),
    .in5(nor_1_out), .in6(not_1_out), .out(ALU_result), .sel(undriven));  // open: in7, en
endmodule

module Reg_File (
  input  [15:0] data_out_1,
  input  [15:0] Data_In,
  input  RegWrite,
  input  [2:0] Read_registrar_1,
  input  [2:0] Write_Address,
  input  [2:0] Read_Registrar_2,
  input  [15:0] data_out_2,
  input  in_8
);

  wire and_1_out, and_2_out, and_3_out, and_4_out, and_5_out, and_6_out, and_7_out, and_8_out,
       decoder_1_out1, decoder_1_out2, decoder_1_out3, decoder_1_out5, decoder_1_out6, decoder_1_out7;
  wire [15:0] register_1_q, register_2_q, register_3_q, register_4_q, register_5_q, register_6_q,
       register_7_q, register_8_q;

  Decoder #(.select(3)) decoder_1 (
    .out0(RegWrite), .out1(decoder_1_out1), .out2(decoder_1_out2), .out3(decoder_1_out3), .out4(RegWrite),
    .out5(decoder_1_out5), .out6(decoder_1_out6), .out7(decoder_1_out7), .sel(Write_Address));  // open: en
  and and_1 (and_1_out, RegWrite, RegWrite);
  and and_2 (and_2_out, RegWrite, decoder_1_out1);
  and and_3 (and_3_out, RegWrite, decoder_1_out2);
  and and_4 (and_4_out, RegWrite, decoder_1_out3);
  and and_5 (and_5_out, RegWrite, RegWrite);
  and and_6 (and_6_out, RegWrite, decoder_1_out5);
  and and_7 (and_7_out, RegWrite, decoder_1_out6);
  and and_8 (and_8_out, RegWrite, decoder_1_out7);
  Register #(.width(16)) register_1 (.D(Data_In), .en(and_1_out), .Q(register_1_q), .clk(in_8));  // open: clr
  Register #(.width(16)) register_2 (.D(Data_In), .en(and_2_out), .Q(register_2_q), .clk(in_8));  // open: clr
  Register #(.width(16)) register_3 (.D(Data_In), .en(and_3_out), .Q(register_3_q), .clk(in_8));  // open: clr
  Register #(.width(16)) register_4 (.D(Data_In), .en(and_4_out), .Q(register_4_q), .clk(in_8));  // open: clr
  Register #(.width(16)) register_5 (.D(Data_In), .en(and_5_out), .Q(register_5_q), .clk(in_8));  // open: clr
  Register #(.width(16)) register_6 (.D(Data_In), .en(and_6_out), .Q(register_6_q), .clk(in_8));  // open: clr
  Register #(.width(16)) register_7 (.D(Data_In), .en(and_7_out), .Q(register_7_q), .clk(in_8));  // open: clr
  Register #(.width(16)) register_8 (.D(Data_In), .en(and_8_out), .Q(register_8_q), .clk(in_8));  // open: clr
  Multiplexer #(.select(3), .width(16)) multiplexer_1 (
    .in0(register_1_q), .in1(register_2_q), .in2(register_3_q), .in3(register_4_q), .in4(register_5_q),
    .in5(register_6_q), .in6(register_7_q), .in7(register_8_q), .out(data_out_1), .sel(Read_registrar_1));  // open: en
  Multiplexer #(.select(3), .width(16)) multiplexer_2 (
    .in0(register_1_q), .in1(register_2_q), .in2(register_3_q), .in3(register_4_q), .in4(register_5_q),
    .in5(register_6_q), .in6(register_7_q), .in7(register_8_q), .out(data_out_2), .sel(Read_Registrar_2));  // open: en
endmodule

module control_unit (
  input  [5:0] in_1,
  input  RegWrite,
  input  [1:0] ALUOp
);

  wire and_2_out, not_1_out, not_2_out, not_3_out, not_4_out, not_5_out, not_6_out, not_7_out, not_8_out,
       not_9_out, not_10_out, not_11_out, not_12_out, not_13_out, not_14_out, not_15_out, not_16_out;

  not not_1 (not_1_out, in_1[1]);
  not not_2 (not_2_out, in_1[2]);
  not not_3 (not_3_out, in_1[3]);
  not not_4 (not_4_out, in_1[4]);
  not not_5 (not_5_out, in_1[0]);
  and and_1 (ALUOp[0], not_5_out, not_1_out, not_2_out, not_3_out, not_4_out, not_6_out);
  not not_6 (not_6_out, in_1[5]);
  not not_7 (not_7_out, in_1[1]);
  not not_8 (not_8_out, in_1[3]);
  not not_9 (not_9_out, in_1[2]);
  and and_2 (and_2_out, in_1[0], not_7_out, not_9_out, not_8_out, in_1[4], in_1[5]);
  not not_10 (not_10_out, in_1[1]);
  // AND_Gate and_3 has open pins: in0=in_1[0], in1=not_10_out, in2=in_1[2], in3=not_11_out, in4=in_1[4], in5=in_1[5], out=open
  not not_11 (not_11_out, in_1[3]);
  not not_12 (not_12_out, in_1[1]);
  not not_13 (not_13_out, in_1[0]);
  not not_14 (not_14_out, in_1[2]);
  and and_4 (ALUOp[1], not_13_out, not_12_out, not_14_out, in_1[3], not_15_out, not_16_out);
  not not_15 (not_15_out, in_1[4]);
  not not_16 (not_16_out, in_1[5]);
  or or_1 (RegWrite, and_2_out, ALUOp[0]);
endmodule

module ALU_control (
  input  [1:0] ALUOp,
  input  [3:0] ALU_Control
);

  wire and_1_out, or_1_out, undriven_2;
  wire [3:0] undriven;

  and and_1 (and_1_out, undriven_2, undriven[1]);
  or or_1 (or_1_out, undriven[3], undriven[0]);
  and and_2 (ALU_Control[2], undriven_2, or_1_out);
  or or_2 (ALU_Control[2], undriven_2, and_1_out);
  or or_3 (ALU_Control[1], ~undriven_2, ~undriven[2]);  // OR_Gate

  assign ALU_Control[0] = ALU_Control[2];
  // also tied to VCC on the sheet: ALU_Control[3]
endmodule
